// Logisim project exercice3.circ as structural Verilog: 1 circuit, main circuit main
module main (
  input  A,
  input  A_2,
  input  B,
  output B_2,
  output C
);

  wire nand_2_out, nand_3_out;

  nand nand_1 (B_2, A, A);
  nand nand_2 (nand_2_out, A_2, A_2);
  nand nand_3 (nand_3_out, B, B);
  nand nand_4 (C, nand_2_out, nand_3_out);

  // Notes on the sheet:
  //   Exercice 3  question 2
  //   Exercice 3  question 1
endmodule
